// Digital circuit Session_21_full_adder.dig as structural Verilog
module Session_21_full_adder (
  input  A,
  input  B,
  input  In,
  output Sum,
  output Out
);

  wire and_1_out, and_2_out, xor_1_out;

  xor xor_1 (xor_1_out, A, B);
  xor xor_2 (Sum, xor_1_out, In);
  and and_1 (and_1_out, In, xor_1_out);
  and and_2 (and_2_out, A, B);
  or or_1 (Out, and_1_out, and_2_out);
endmodule
